// Logisim project index.circ as structural Verilog
module HA (
  input  A,
  input  B,
  output sum,
  output carry
);

  xor xor_1 (sum, A, B);
  and and_1 (carry, A, B);
endmodule
